# Fritzing sketch BB-Wiring (saved by Fritzing 0.9.7b)
breadboards: 1

parts:
  Mod1 = Raspberry Pi Pico
  S1 = Pushbutton [package="[THT]"]
  TM1638_Led_and_Key1 = TM1638_Led_and_Key [package=THT]
  TM1638_Led_and_Key2 = TM1638_Led_and_Key [package=THT]

nets:
  GND: Mod1.pin_3, Mod1.pin_8, Mod1.pin_13, Mod1.pin_18, Mod1.pin_23, Mod1.pin_28, Mod1.pin_33, Mod1.pin_38, Mod1.pin_42, S1.Pin_3, S1.Pin_4, TM1638_Led_and_Key1.GND, TM1638_Led_and_Key2.GND
  N1: Mod1.pin_7, TM1638_Led_and_Key1.STB
  N2: Mod1.pin_9, TM1638_Led_and_Key2.STB
  N3: Mod1.pin_10, TM1638_Led_and_Key1.CLK, TM1638_Led_and_Key2.CLK
  N4: Mod1.pin_11, TM1638_Led_and_Key1.DIO, TM1638_Led_and_Key2.DIO
  N5: Mod1.pin_30, S1.Pin_1, S1.Pin_2
  VCC: Mod1.pin_36, TM1638_Led_and_Key1.VCC, TM1638_Led_and_Key2.VCC

custom parts:
  Raspberry Pi Pico: Raspberry Pi Pico. Based around the RP2040 microcontroller the Pico is a low cost microcontroller device bringing Raspberry Pi quality, cost, and easy of use to the microcontroller space. Jan 2021, Split part in to two versions: tht (this one) and SMD. This one will drill holes for a .1 in header in pcb to allow plugging in the module as well as providing pads to solder the module to the top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
